// Logisim project Task4.circ as structural Verilog: 1 circuit, main circuit main
module main (
  input  EN,
  output [1:0] out_2
);

  wire and_1_out, and_2_out, clock_1_out, d_ff_1_qn, multiplexer_1_out, multiplexer_2_out, not_1_out,
       not_2_out, or_1_out, or_2_out;

  or or_1 (or_1_out, not_1_out, out_2[1]);
  not not_1 (not_1_out, out_2[0]);
  D_Flip_Flop d_ff_1 (.D(multiplexer_1_out), .clk(clock_1_out), .Q(out_2[0]), .Qn(d_ff_1_qn));  // open: preset, reset
  Multiplexer multiplexer_1 (.in0(or_1_out), .in1(and_1_out), .out(multiplexer_1_out), .sel(not_2_out));
  and and_1 (and_1_out, d_ff_1_qn, out_2[1]);
  Clock clock_1 (.out(clock_1_out));
  or or_2 (or_2_out, out_2[1], out_2[0]);
  and and_2 (and_2_out, out_2[0], out_2[1]);
  not not_2 (not_2_out, EN);
  Multiplexer multiplexer_2 (.in0(or_2_out), .in1(and_2_out), .out(multiplexer_2_out), .sel(not_2_out));
  D_Flip_Flop d_ff_2 (.D(multiplexer_2_out), .clk(clock_1_out), .Q(out_2[1]));  // open: Qn, preset, reset
endmodule
