// Logisim project rv32e_core_assign.circ as structural Verilog: 25 circuits, main circuit core
module SoC_sim_v2 (
  input  RST,
  output uart_tx,
  output [31:0] gpio_out_en
);

  wire and_1_out, C, core_1_mem_wr, decoder_1_out0, decoder_1_out1, decoder_1_out2, decoder_1_out3;
  wire [1:0] core_1_addr;
  wire [2:0] core_1_strobe;
  wire [11:0] core_1_addr_2;
  wire [15:0] core_1_mem_wr_data, core_1_mem_wr_data_2, uart_v2_1_rd_data;
  wire [15:14] core_1_addr_3;
  wire [31:0] button_1_out, gpio_1_gpio_out, gpio_1_rd_data, main_memory_data_out, multiplexer_1_out;

  Clock clock_1 (.out(C));
  core core_1 (
    .mem_rd_data(multiplexer_1_out), .clk(C), .rst(RST), .mem_wr(core_1_mem_wr),
    .mem_wr_data({core_1_mem_wr_data_2, core_1_mem_wr_data}),
    .addr({core_1_addr_3, core_1_addr_2, core_1_addr}), .strobe(core_1_strobe));
  Decoder #(.enable("false"), .select(2)) decoder_1 (
    .out0(decoder_1_out0), .out1(decoder_1_out1), .out2(decoder_1_out2), .out3(decoder_1_out3),
    .sel(core_1_addr_3));
  and and_1 (and_1_out, core_1_mem_wr, decoder_1_out3);
  TTY tty_1 (.data(core_1_mem_wr_data[6:0]), .clk(C), .we(and_1_out), .clr(RST));
  memory main_memory (
    .data_in({core_1_mem_wr_data_2, core_1_mem_wr_data}), .addr({core_1_addr_2, core_1_addr}),
    .slave_en(decoder_1_out0), .wr_en(core_1_mem_wr), .strobe(core_1_strobe), .clk(C),
    .data_out(main_memory_data_out));
  uart_v2 uart_v2_1 (
    .clk(C), .rst(RST), .slave_en(decoder_1_out1), .addr(core_1_addr), .write_data(core_1_mem_wr_data),
    .write_en(core_1_mem_wr), .rd_data(uart_v2_1_rd_data), .tx(uart_tx));
  gpio gpio_1 (
    .clk(C), .rst(RST), .gpio_in(button_1_out), .slave_en(decoder_1_out2),
    .addr({core_1_addr_2[1:0], core_1_addr}), .write_data({core_1_mem_wr_data_2, core_1_mem_wr_data}),
    .write_en(core_1_mem_wr), .rd_data(gpio_1_rd_data), .gpio_out(gpio_1_gpio_out), .gpio_out_en(gpio_out_en));
  Multiplexer #(.select(2), .width(32)) multiplexer_1 (
    .in0(main_memory_data_out), .in1({{16{1'b0}}, uart_v2_1_rd_data}), .in2(gpio_1_rd_data),
    .in3({32{1'b0}}), .out(multiplexer_1_out), .sel(core_1_addr_3));
  // Probe on gpio_1_gpio_out[7:0]
  // Probe on gpio_1_gpio_out[15:8]
  DotMatrix #(.inputtype("row"), .matrixcols(8), .matrixrows(4)) dotmatrix_1 (
    .row0(gpio_1_gpio_out[7:0]), .row1(gpio_1_gpio_out[15:8]), .row2(gpio_1_gpio_out[23:16]),
    .row3(gpio_1_gpio_out[31:24]));
  Button button_1 (.out(button_1_out[0]));
  Button button_2 (.out(button_1_out[3]));
  Button button_3 (.out(button_1_out[1]));
  Button button_4 (.out(button_1_out[2]));

  // Other names for the same wires on the sheet: R = RST
endmodule

module core (
  input  [31:0] mem_rd_data,
  input  clk,
  input  rst,
  output mem_wr,
  output [31:0] mem_wr_data,
  output [15:0] addr,
  output [2:0] strobe
);

  wire alu_v1_1_branch_cond, control_unit_1_addr_inst_or_data, control_unit_1_data_wb_or_load,
       control_unit_1_decode_exe, control_unit_1_decode_in, control_unit_1_fetch, control_unit_1_funct3_sel,
       control_unit_1_funct7_sel, control_unit_1_j_4, control_unit_1_mem, control_unit_1_opcode_a_sel,
       control_unit_1_pc_in_en, control_unit_1_rf_rd_in_en, control_unit_1_rs1_sel, control_unit_1_rs2_sel,
       control_unit_1_write_back, j_sell, jalr_pc, not_1_out;
  wire [1:0] control_unit_1_inc_pc, control_unit_1_opcode_b_sel;
  wire [2:0] idecoder_1_funct3, idecoder_1_funct3_cntrl;
  wire [4:0] idecoder_1_rd, idecoder_1_rs1, idecoder_1_rs2;
  wire [5:0] idecoder_1_funct7;
  wire [5:5] idecoder_1_funct7_2;
  wire [8:0] idecoder_1_ins_type_decode;
  wire [15:0] alu_v1_1_alu_addr_out, alu_v1_1_alu_addr_out_2, rg_pc_q_2;
  wire [15:2] rg_pc_q;
  wire [31:0] adder_1_out, adder_2_out, adder_3_out, idecoder_1_b_type_imm, idecoder_1_j_type_imm,
       idecoder_1_s_type_imm, idecoder_1_u_type_imm, inc, jalr_imm, jalr_rs1, multiplexer_1_out,
       multiplexer_3_out, multiplexer_4_out, multiplexer_5_out, multiplexer_6_out, multiplexer_7_out;

  Adder #(.width(32)) adder_1 (.a({rg_pc_q_2, rg_pc_q, 2'b00}), .b(inc), .out(adder_1_out), .cin(1'b0));  // open: cout
  Adder #(.width(32)) adder_2 (
    .a(32'h4), .b({rg_pc_q_2, rg_pc_q, 2'b00}), .out(adder_2_out), .cin(1'b0));  // open: cout
  // Probe on {rg_pc_q_2, rg_pc_q, 2'b00}
  // Probe on multiplexer_1_out
  Multiplexer #(.width(32)) multiplexer_1 (
    .in0(adder_1_out), .in1(adder_3_out), .out(multiplexer_1_out), .sel(jalr_pc));
  Adder #(.width(32)) adder_3 (.a(jalr_rs1), .b(jalr_imm), .out(adder_3_out), .cin(1'b0));  // open: cout
  Register #(.width(30)) rg_pc (
    .D(multiplexer_1_out[31:2]), .en(control_unit_1_pc_in_en), .clk(clk), .Q({rg_pc_q_2, rg_pc_q}), .clr(rst));
  idecoder idecoder_1 (
    .instruction(mem_rd_data), .funct3_sel(control_unit_1_funct3_sel), .rs1_sel(control_unit_1_rs1_sel),
    .rs2_sel(control_unit_1_rs2_sel), .funct7_sel(control_unit_1_funct7_sel),
    .decode_en(control_unit_1_decode_in), .clk(clk), .rst(rst), .rd(idecoder_1_rd),
    .funct3(idecoder_1_funct3), .rs1(idecoder_1_rs1), .rs2(idecoder_1_rs2),
    .funct7({idecoder_1_funct7[5], idecoder_1_funct7_2[5], idecoder_1_funct7[4:0]}),
    .u_type_imm(idecoder_1_u_type_imm), .s_type_imm(idecoder_1_s_type_imm), .I_type_imm(jalr_imm),
    .J_type_imm(idecoder_1_j_type_imm), .B_type_imm(idecoder_1_b_type_imm),
    .ins_type_decode(idecoder_1_ins_type_decode), .funct3_cntrl(idecoder_1_funct3_cntrl));
  control_unit control_unit_1 (
    .C(clk), .R(rst), .funct3(idecoder_1_funct3_cntrl), .inst_type_decode(idecoder_1_ins_type_decode),
    .b_c(alu_v1_1_branch_cond), .pc_in_en(control_unit_1_pc_in_en),
    .addr_inst_or_data(control_unit_1_addr_inst_or_data), .funct3_sel(control_unit_1_funct3_sel),
    .rs1_sel(control_unit_1_rs1_sel), .rs2_sel(control_unit_1_rs2_sel),
    .funct7_sel(control_unit_1_funct7_sel), .opcode_a_sel(control_unit_1_opcode_a_sel),
    .opcode_b_sel(control_unit_1_opcode_b_sel), .mem_wr_en_cntrl(mem_wr),
    .rf_rd_in_en(control_unit_1_rf_rd_in_en), .data_wb_or_load(control_unit_1_data_wb_or_load),
    .mem_strobe(strobe), .decode_in(control_unit_1_decode_in), .fetch(control_unit_1_fetch),
    .decode_exe(control_unit_1_decode_exe), .mem(control_unit_1_mem), .write_back(control_unit_1_write_back),
    .J_4(control_unit_1_j_4), .inc_pc(control_unit_1_inc_pc), .jalr(jalr_pc), .j_sel(j_sell));
  LED LED_3 (.in(control_unit_1_decode_exe));
  LED LED_4 (.in(control_unit_1_fetch));
  Multiplexer #(.width(16)) multiplexer_2 (
    .in0({rg_pc_q, 2'b00}), .in1(alu_v1_1_alu_addr_out), .out(addr), .sel(control_unit_1_addr_inst_or_data));
  LED LED_1 (.in(control_unit_1_write_back));
  LED LED_2 (.in(control_unit_1_mem));
  Multiplexer #(.width(32)) multiplexer_3 (
    .in0({alu_v1_1_alu_addr_out_2, alu_v1_1_alu_addr_out}), .in1(mem_rd_data), .out(multiplexer_3_out),
    .sel(control_unit_1_data_wb_or_load));
  Multiplexer #(.width(32)) multiplexer_4 (
    .in0(adder_2_out), .in1(multiplexer_3_out), .out(multiplexer_4_out), .sel(not_1_out));
  not not_1 (not_1_out, j_sell);
  regfile16x32 regfile16x32_1 (
    .rs2_sel(idecoder_1_rs2), .rs1_sel(idecoder_1_rs1), .rd_wr_sel(idecoder_1_rd),
    .rd_wr_en(control_unit_1_rf_rd_in_en), .rd_wr_val(multiplexer_4_out), .clk(clk), .rst(rst),
    .rs1_val(jalr_rs1), .rs2_val(mem_wr_data));
  Multiplexer #(.width(32)) multiplexer_5 (
    .in0(jalr_rs1), .in1({rg_pc_q_2, rg_pc_q, 2'b00}), .out(multiplexer_5_out),
    .sel(control_unit_1_opcode_a_sel));
  Multiplexer #(.select(2), .width(32)) multiplexer_6 (
    .in0(mem_wr_data), .in1(idecoder_1_u_type_imm), .in2(idecoder_1_s_type_imm), .in3(jalr_imm),
    .out(multiplexer_6_out), .sel(control_unit_1_opcode_b_sel));
  Multiplexer #(.width(32)) multiplexer_7 (
    .in0(multiplexer_6_out), .in1(32'h4), .out(multiplexer_7_out), .sel(control_unit_1_j_4));
  Multiplexer #(.select(2), .width(32)) multiplexer_8 (
    .in0(32'h4), .in1(idecoder_1_b_type_imm), .in2(idecoder_1_j_type_imm), .in3(32'h4), .out(inc),
    .sel(control_unit_1_inc_pc));
  alu_v1 alu_v1_1 (
    .a_input(multiplexer_5_out), .b_input(multiplexer_7_out), .func_7(idecoder_1_funct7_2[5]),
    .func_3(idecoder_1_funct3), .rs1_a(jalr_rs1), .rs2_a(mem_wr_data),
    .ALU_ADDR_OUT({alu_v1_1_alu_addr_out_2, alu_v1_1_alu_addr_out}), .branch_cond(alu_v1_1_branch_cond));

  // Other names for the same wires on the sheet: C = clk; R = rst
endmodule

// decoder
module idecoder (
  input  [31:0] instruction,
  input  funct3_sel,
  input  rs1_sel,
  input  rs2_sel,
  input  funct7_sel,
  input  decode_en,
  input  clk,
  input  rst,
  output [4:0] rd,
  output [2:0] funct3,
  output [4:0] rs1,
  output [4:0] rs2,
  output [6:0] funct7,
  output [31:0] u_type_imm,
  output [31:0] s_type_imm,
  output [31:0] I_type_imm,
  output [31:0] J_type_imm,
  output [31:0] B_type_imm,
  output [8:0] ins_type_decode,
  output [2:0] funct3_cntrl
);

  wire [6:0] opcode;

  Register #(.width(32)) rg_decode (
    .D(instruction), .en(decode_en), .clk(clk),
    .Q({B_type_imm[12], B_type_imm[10:5], I_type_imm[4:0], J_type_imm[19:15], funct3_cntrl, B_type_imm[4:1], B_type_imm[11], opcode}),
    .clr(rst));
  assign J_type_imm[31:20] = {{11{B_type_imm[12]}}, B_type_imm[12]};  // Bit_Extender bit_extender_1
  Multiplexer #(.width(3)) multiplexer_1 (.in0(funct3_cntrl), .in1(3'b000), .out(funct3), .sel(funct3_sel));
  Multiplexer #(.width(5)) multiplexer_2 (.in0(J_type_imm[19:15]), .in1({5{1'b0}}), .out(rs1), .sel(rs1_sel));
  Multiplexer #(.width(5)) multiplexer_3 (.in0({5{1'b0}}), .in1(I_type_imm[4:0]), .out(rs2), .sel(rs2_sel));
  Multiplexer #(.width(7)) multiplexer_4 (
    .in0({7{1'b0}}), .in1({B_type_imm[12], B_type_imm[10:5]}), .out(funct7), .sel(funct7_sel));
  assign I_type_imm[31:11] = {{20{B_type_imm[12]}}, B_type_imm[12]};  // Bit_Extender bit_extender_2
  Comparator #(.mode("unsigned"), .width(7)) comparator_1 (
    .a(opcode), .b(7'b0110111), .eq(ins_type_decode[0]));  // open: gt, lt
  Comparator #(.mode("unsigned"), .width(7)) comparator_2 (
    .a(opcode), .b(7'b0010111), .eq(ins_type_decode[1]));  // open: gt, lt
  Comparator #(.mode("unsigned"), .width(7)) comparator_3 (
    .a(opcode), .b(7'b0000011), .eq(ins_type_decode[5]));  // open: gt, lt
  Comparator #(.mode("unsigned"), .width(7)) comparator_4 (
    .a(opcode), .b(7'b0100011), .eq(ins_type_decode[6]));  // open: gt, lt
  Comparator #(.mode("unsigned"), .width(7)) comparator_5 (
    .a(opcode), .b(7'b0010011), .eq(ins_type_decode[7]));  // open: gt, lt
  Comparator #(.mode("unsigned"), .width(7)) comparator_6 (
    .a(opcode), .b(7'b0110011), .eq(ins_type_decode[8]));  // open: gt, lt
  assign u_type_imm[11:0] = {{11{1'b0}}, 1'b0};  // Bit_Extender bit_extender_3
  Comparator #(.mode("unsigned"), .width(7)) comparator_7 (
    .a(opcode), .b(7'b1100011), .eq(ins_type_decode[2]));  // open: gt, lt
  Comparator #(.mode("unsigned"), .width(7)) comparator_8 (
    .a(opcode), .b(7'b1101111), .eq(ins_type_decode[3]));  // open: gt, lt
  assign B_type_imm[31:13] = {{18{B_type_imm[12]}}, B_type_imm[12]};  // Bit_Extender bit_extender_4
  Comparator #(.mode("unsigned"), .width(7)) comparator_9 (
    .a(opcode), .b(7'b1100111), .eq(ins_type_decode[4]));  // open: gt, lt

  assign B_type_imm[0] = 1'b0;
  assign I_type_imm[10:5] = B_type_imm[10:5];
  assign J_type_imm[14:0] = {funct3_cntrl, I_type_imm[0], B_type_imm[10:5], I_type_imm[4:1], 1'b0};
  assign rd = {B_type_imm[4:1], B_type_imm[11]};
  assign s_type_imm = {I_type_imm[31:11], B_type_imm[10:1], B_type_imm[11]};
  assign u_type_imm[31:12] = {B_type_imm[12], B_type_imm[10:5], I_type_imm[4:0], J_type_imm[19:15], funct3_cntrl};

  // Other names for the same wires on the sheet: rd_4[3:0] = B_type_imm[4:1];
  //   f7[6:0] = {B_type_imm[12], B_type_imm[10:5]}; f7_6[5:0] = B_type_imm[10:5]; rd_1 = B_type_imm[11];
  //   f7_1 = B_type_imm[12]; rs2_4[3:0] = I_type_imm[4:1]; rs2_t[4:0] = I_type_imm[4:0]; rs2_1 = I_type_imm[0];
  //   f3[2:0] = funct3_cntrl; rs1_t[4:0] = J_type_imm[19:15]

  // Notes on the sheet:
  //   31 (1) funct7 / imm
  //   0-6 (7) opcode
  //   7 (1) rd / imm
  //   8-11 (4) rd / imm
  //   12-14 (3) funct3 / imm 
  //   15 -19 (5) rs1/ imm
  //   21-24 (4) rs2 / imm
  //   25-30 (6) funct7/ imm
  //   20 (1) rs2 / imm
  //   u_type_lui
  //   u_type_auipc
  //   i_type_load
  //   s_type_store
  //   i_type
  //   r_type
  //   b_branch
  //   j_jal
  //   i_jalr
endmodule

// regfile32
module regfile32x32 (
  input  [4:0] read_register_1,
  input  write_enable,
  input  [4:0] write_register,
  input  [31:0] write_data,
  input  clk,
  input  rst,
  input  [4:0] read_register_2,
  output [31:0] read_data_1,
  output [31:0] read_data_2
);

  wire decoder_1_out0, decoder_1_out1, decoder_1_out2, decoder_1_out3, decoder_1_out4, decoder_1_out5,
       decoder_1_out6, decoder_1_out7, decoder_1_out8, decoder_1_out9, decoder_1_out10, decoder_1_out11,
       decoder_1_out12, decoder_1_out13, decoder_1_out14, decoder_1_out15, decoder_1_out16, decoder_1_out17,
       decoder_1_out18, decoder_1_out19, decoder_1_out20, decoder_1_out21, decoder_1_out22, decoder_1_out23,
       decoder_1_out24, decoder_1_out25, decoder_1_out26, decoder_1_out27, decoder_1_out28, decoder_1_out29,
       decoder_1_out30, decoder_1_out31;
  wire [31:0] register_1_q, register_2_q, register_3_q, register_4_q, register_5_q, register_6_q,
       register_7_q, register_8_q, register_9_q, register_10_q, register_11_q, register_12_q, register_13_q,
       register_14_q, register_15_q, register_16_q, register_17_q, register_18_q, register_19_q,
       register_20_q, register_21_q, register_22_q, register_23_q, register_24_q, register_25_q,
       register_26_q, register_27_q, register_28_q, register_29_q, register_30_q, register_31_q;

  Decoder #(.select(5)) decoder_1 (
    .out0(decoder_1_out0), .out1(decoder_1_out1), .out2(decoder_1_out2), .out3(decoder_1_out3),
    .out4(decoder_1_out4), .out5(decoder_1_out5), .out6(decoder_1_out6), .out7(decoder_1_out7),
    .out8(decoder_1_out8), .out9(decoder_1_out9), .out10(decoder_1_out10), .out11(decoder_1_out11),
    .out12(decoder_1_out12), .out13(decoder_1_out13), .out14(decoder_1_out14), .out15(decoder_1_out15),
    .out16(decoder_1_out16), .out17(decoder_1_out17), .out18(decoder_1_out18), .out19(decoder_1_out19),
    .out20(decoder_1_out20), .out21(decoder_1_out21), .out22(decoder_1_out22), .out23(decoder_1_out23),
    .out24(decoder_1_out24), .out25(decoder_1_out25), .out26(decoder_1_out26), .out27(decoder_1_out27),
    .out28(decoder_1_out28), .out29(decoder_1_out29), .out30(decoder_1_out30), .out31(decoder_1_out31),
    .sel(write_register), .en(write_enable));
  Register #(.width(32)) register_1 (.D(write_data), .en(decoder_1_out8), .clk(clk), .Q(register_1_q), .clr(rst));
  Register #(.width(32)) register_2 (.D(write_data), .en(decoder_1_out16), .clk(clk), .Q(register_2_q), .clr(rst));
  Register #(.width(32)) register_3 (.D(write_data), .en(decoder_1_out24), .clk(clk), .Q(register_3_q), .clr(rst));
  Register #(.width(32)) register_4 (.D(write_data), .en(decoder_1_out1), .clk(clk), .Q(register_4_q), .clr(rst));
  Register #(.width(32)) register_5 (.D(write_data), .en(decoder_1_out9), .clk(clk), .Q(register_5_q), .clr(rst));
  Register #(.width(32)) register_6 (.D(write_data), .en(decoder_1_out17), .clk(clk), .Q(register_6_q), .clr(rst));
  Register #(.width(32)) register_7 (.D(write_data), .en(decoder_1_out25), .clk(clk), .Q(register_7_q), .clr(rst));
  Register #(.width(32)) register_8 (.D(write_data), .en(decoder_1_out2), .clk(clk), .Q(register_8_q), .clr(rst));
  Register #(.width(32)) register_9 (.D(write_data), .en(decoder_1_out10), .clk(clk), .Q(register_9_q), .clr(rst));
  Register #(.width(32)) register_10 (.D(write_data), .en(decoder_1_out18), .clk(clk), .Q(register_10_q), .clr(rst));
  Register #(.width(32)) register_11 (.D(write_data), .en(decoder_1_out26), .clk(clk), .Q(register_11_q), .clr(rst));
  Register #(.width(32)) register_12 (.D(write_data), .en(decoder_1_out3), .clk(clk), .Q(register_12_q), .clr(rst));
  Register #(.width(32)) register_13 (.D(write_data), .en(decoder_1_out11), .clk(clk), .Q(register_13_q), .clr(rst));
  Register #(.width(32)) register_14 (.D(write_data), .en(decoder_1_out19), .clk(clk), .Q(register_14_q), .clr(rst));
  Register #(.width(32)) register_15 (.D(write_data), .en(decoder_1_out27), .clk(clk), .Q(register_15_q), .clr(rst));
  Register #(.width(32)) register_16 (.D(write_data), .en(decoder_1_out4), .clk(clk), .Q(register_16_q), .clr(rst));
  Register #(.width(32)) register_17 (.D(write_data), .en(decoder_1_out12), .clk(clk), .Q(register_17_q), .clr(rst));
  Register #(.width(32)) register_18 (.D(write_data), .en(decoder_1_out20), .clk(clk), .Q(register_18_q), .clr(rst));
  Register #(.width(32)) register_19 (.D(write_data), .en(decoder_1_out28), .clk(clk), .Q(register_19_q), .clr(rst));
  Register #(.width(32)) register_20 (.D(write_data), .en(decoder_1_out5), .clk(clk), .Q(register_20_q), .clr(rst));
  Register #(.width(32)) register_21 (.D(write_data), .en(decoder_1_out13), .clk(clk), .Q(register_21_q), .clr(rst));
  Register #(.width(32)) register_22 (.D(write_data), .en(decoder_1_out21), .clk(clk), .Q(register_22_q), .clr(rst));
  Register #(.width(32)) register_23 (.D(write_data), .en(decoder_1_out29), .clk(clk), .Q(register_23_q), .clr(rst));
  Register #(.width(32)) register_24 (.D(write_data), .en(decoder_1_out6), .clk(clk), .Q(register_24_q), .clr(rst));
  Register #(.width(32)) register_25 (.D(write_data), .en(decoder_1_out14), .clk(clk), .Q(register_25_q), .clr(rst));
  Register #(.width(32)) register_26 (.D(write_data), .en(decoder_1_out22), .clk(clk), .Q(register_26_q), .clr(rst));
  Register #(.width(32)) register_27 (.D(write_data), .en(decoder_1_out30), .clk(clk), .Q(register_27_q), .clr(rst));
  Register #(.width(32)) register_28 (.D(write_data), .en(decoder_1_out7), .clk(clk), .Q(register_28_q), .clr(rst));
  Register #(.width(32)) register_29 (.D(write_data), .en(decoder_1_out15), .clk(clk), .Q(register_29_q), .clr(rst));
  Register #(.width(32)) register_30 (.D(write_data), .en(decoder_1_out23), .clk(clk), .Q(register_30_q), .clr(rst));
  Register #(.width(32)) register_31 (.D(write_data), .en(decoder_1_out31), .clk(clk), .Q(register_31_q), .clr(rst));
  Multiplexer #(.select(5), .width(32)) multiplexer_1 (
    .in0({32{1'b0}}), .in1(register_4_q), .in2(register_8_q), .in3(register_12_q), .in4(register_16_q),
    .in5(register_20_q), .in6(register_24_q), .in7(register_28_q), .in8(register_1_q), .in9(register_5_q),
    .in10(register_9_q), .in11(register_13_q), .in12(register_17_q), .in13(register_21_q),
    .in14(register_25_q), .in15(register_29_q), .in16(register_2_q), .in17(register_6_q),
    .in18(register_10_q), .in19(register_14_q), .in20(register_18_q), .in21(register_22_q),
    .in22(register_26_q), .in23(register_30_q), .in24(register_3_q), .in25(register_7_q),
    .in26(register_11_q), .in27(register_15_q), .in28(register_19_q), .in29(register_23_q),
    .in30(register_27_q), .in31(register_31_q), .out(read_data_1), .sel(read_register_1));
  Multiplexer #(.select(5), .width(32)) multiplexer_2 (
    .in0({32{1'b0}}), .in1(register_4_q), .in2(register_8_q), .in3(register_12_q), .in4(register_16_q),
    .in5(register_20_q), .in6(register_24_q), .in7(register_28_q), .in8(register_1_q), .in9(register_5_q),
    .in10(register_9_q), .in11(register_13_q), .in12(register_17_q), .in13(register_21_q),
    .in14(register_25_q), .in15(register_29_q), .in16(register_2_q), .in17(register_6_q),
    .in18(register_10_q), .in19(register_14_q), .in20(register_18_q), .in21(register_22_q),
    .in22(register_26_q), .in23(register_30_q), .in24(register_3_q), .in25(register_7_q),
    .in26(register_11_q), .in27(register_15_q), .in28(register_19_q), .in29(register_23_q),
    .in30(register_27_q), .in31(register_31_q), .out(read_data_2), .sel(read_register_2));
endmodule

// regfile16
module regfile16x32 (
  input  rd_wr_en,
  input  [31:0] rd_wr_val,
  input  [4:0] rd_wr_sel,
  input  [4:0] rs1_sel,
  input  [4:0] rs2_sel,
  input  clk,
  input  rst,
  output [31:0] rs1_val,
  output [31:0] rs2_val
);

  wire decoder_1_out0, decoder_1_out1, decoder_1_out2, decoder_1_out3, decoder_1_out4, decoder_1_out5,
       decoder_1_out6, decoder_1_out7, decoder_1_out8, decoder_1_out9, decoder_1_out10, decoder_1_out11,
       decoder_1_out12, decoder_1_out13, decoder_1_out14, decoder_1_out15;
  wire [31:0] x1_q, x2_q, x3_q, x4_q, x5_q, x6_q, x7_q, x8_q, x9_q, x10_q, x11_q, x12_q, x13_q, x14_q, x15_q;

  Decoder #(.select(4)) decoder_1 (
    .out0(decoder_1_out0), .out1(decoder_1_out1), .out2(decoder_1_out2), .out3(decoder_1_out3),
    .out4(decoder_1_out4), .out5(decoder_1_out5), .out6(decoder_1_out6), .out7(decoder_1_out7),
    .out8(decoder_1_out8), .out9(decoder_1_out9), .out10(decoder_1_out10), .out11(decoder_1_out11),
    .out12(decoder_1_out12), .out13(decoder_1_out13), .out14(decoder_1_out14), .out15(decoder_1_out15),
    .sel(rd_wr_sel[3:0]), .en(rd_wr_en));
  Register #(.width(32)) x8 (.D(rd_wr_val), .en(decoder_1_out8), .clk(clk), .Q(x8_q), .clr(rst));
  Register #(.width(32)) x1 (.D(rd_wr_val), .en(decoder_1_out1), .clk(clk), .Q(x1_q), .clr(rst));
  Register #(.width(32)) x9 (.D(rd_wr_val), .en(decoder_1_out9), .clk(clk), .Q(x9_q), .clr(rst));
  Register #(.width(32)) x2 (.D(rd_wr_val), .en(decoder_1_out2), .clk(clk), .Q(x2_q), .clr(rst));
  Register #(.width(32)) x10 (.D(rd_wr_val), .en(decoder_1_out10), .clk(clk), .Q(x10_q), .clr(rst));
  Register #(.width(32)) x3 (.D(rd_wr_val), .en(decoder_1_out3), .clk(clk), .Q(x3_q), .clr(rst));
  Register #(.width(32)) x11 (.D(rd_wr_val), .en(decoder_1_out11), .clk(clk), .Q(x11_q), .clr(rst));
  Register #(.width(32)) x4 (.D(rd_wr_val), .en(decoder_1_out4), .clk(clk), .Q(x4_q), .clr(rst));
  Register #(.width(32)) x12 (.D(rd_wr_val), .en(decoder_1_out12), .clk(clk), .Q(x12_q), .clr(rst));
  Register #(.width(32)) x5 (.D(rd_wr_val), .en(decoder_1_out5), .clk(clk), .Q(x5_q), .clr(rst));
  Register #(.width(32)) x13 (.D(rd_wr_val), .en(decoder_1_out13), .clk(clk), .Q(x13_q), .clr(rst));
  Register #(.width(32)) x6 (.D(rd_wr_val), .en(decoder_1_out6), .clk(clk), .Q(x6_q), .clr(rst));
  Register #(.width(32)) x14 (.D(rd_wr_val), .en(decoder_1_out14), .clk(clk), .Q(x14_q), .clr(rst));
  Register #(.width(32)) x7 (.D(rd_wr_val), .en(decoder_1_out7), .clk(clk), .Q(x7_q), .clr(rst));
  Register #(.width(32)) x15 (.D(rd_wr_val), .en(decoder_1_out15), .clk(clk), .Q(x15_q), .clr(rst));
  Multiplexer #(.select(4), .width(32)) multiplexer_1 (
    .in0({32{1'b0}}), .in1(x1_q), .in2(x2_q), .in3(x3_q), .in4(x4_q), .in5(x5_q), .in6(x6_q), .in7(x7_q),
    .in8(x8_q), .in9(x9_q), .in10(x10_q), .in11(x11_q), .in12(x12_q), .in13(x13_q), .in14(x14_q),
    .in15(x15_q), .out(rs1_val), .sel(rs1_sel[3:0]));
  Multiplexer #(.select(4), .width(32)) multiplexer_2 (
    .in0({32{1'b0}}), .in1(x1_q), .in2(x2_q), .in3(x3_q), .in4(x4_q), .in5(x5_q), .in6(x6_q), .in7(x7_q),
    .in8(x8_q), .in9(x9_q), .in10(x10_q), .in11(x11_q), .in12(x12_q), .in13(x13_q), .in14(x14_q),
    .in15(x15_q), .out(rs2_val), .sel(rs2_sel[3:0]));
endmodule

module alu_v1 (
  input  [31:0] a_input,
  input  [31:0] b_input,
  input  func_7,
  input  [2:0] func_3,
  input  [31:0] rs1_a,
  input  [31:0] rs2_a,
  output [31:0] ALU_ADDR_OUT,
  output branch_cond
);

  wire comparator_1_eq, comparator_1_lt, comparator_2_lt, not_2_out, not_3_out, not_4_out;
  wire [0:0] comparator_3_lt, comparator_4_lt;
  wire [31:0] adder_1_out, and_1_out, multiplexer_1_out, multiplexer_2_out, not_1_out, or_1_out,
       shifter_1_out, shifter_2_out, shifter_3_out, xor_1_out;

  // Probe on a_input
  // Probe on a_input
  // Probe on a_input
  Comparator #(.width(32)) comparator_1 (.a(rs1_a), .b(rs2_a), .eq(comparator_1_eq), .lt(comparator_1_lt));  // open: gt
  Comparator #(.mode("unsigned"), .width(32)) comparator_2 (
    .a(rs1_a), .b(rs2_a), .lt(comparator_2_lt));  // open: gt, eq
  Multiplexer #(.width(32)) multiplexer_1 (.in0(b_input), .in1(not_1_out), .out(multiplexer_1_out), .sel(func_7));
  assign not_1_out = ~b_input;  // NOT_Gate not_1, 32 bits wide
  Adder #(.width(32)) adder_1 (.a(a_input), .b(multiplexer_1_out), .out(adder_1_out), .cin(func_7));  // open: cout
  Shifter #(.width(32)) shifter_1 (.in(a_input), .\dist (b_input[4:0]), .out(shifter_1_out));
  Comparator #(.width(32)) comparator_3 (.a(a_input), .b(b_input), .lt(comparator_3_lt[0]));  // open: gt, eq
  Comparator #(.mode("unsigned"), .width(32)) comparator_4 (
    .a(a_input), .b(b_input), .lt(comparator_4_lt[0]));  // open: gt, eq
  assign xor_1_out = b_input ^ a_input;  // XOR_Gate xor_1, 32 bits wide
  Shifter #(.shift("lr"), .width(32)) shifter_2 (.in(a_input), .\dist (b_input[4:0]), .out(shifter_2_out));
  Multiplexer #(.width(32)) multiplexer_2 (
    .in0(shifter_2_out), .in1(shifter_3_out), .out(multiplexer_2_out), .sel(func_7));
  Shifter #(.shift("ar"), .width(32)) shifter_3 (.in(a_input), .\dist (b_input[4:0]), .out(shifter_3_out));
  assign or_1_out = a_input | b_input;  // OR_Gate or_1, 32 bits wide
  assign and_1_out = a_input & b_input;  // AND_Gate and_1, 32 bits wide
  // Probe on b_input
  // Probe on b_input
  // Probe on b_input
  not not_2 (not_2_out, comparator_1_eq);
  not not_3 (not_3_out, comparator_1_lt);
  // Probe on adder_1_out
  // Probe on adder_1_out
  // Probe on adder_1_out
  not not_4 (not_4_out, comparator_2_lt);
  Multiplexer #(.select(3)) multiplexer_3 (
    .in0(comparator_1_eq), .in1(not_2_out), .in2(1'b0), .in3(1'b0), .in4(comparator_1_lt), .in5(not_3_out),
    .in6(comparator_2_lt), .in7(not_4_out), .out(branch_cond), .sel(func_3));
  Multiplexer #(.select(3), .width(32)) multiplexer_4 (
    .in0(adder_1_out), .in1(shifter_1_out), .in2({{31{1'b0}}, comparator_3_lt[0]}),
    .in3({{31{1'b0}}, comparator_4_lt[0]}), .in4(xor_1_out), .in5(multiplexer_2_out), .in6(or_1_out),
    .in7(and_1_out), .out(ALU_ADDR_OUT), .sel(func_3));

  // Notes on the sheet:
  //   6). 110 --> OR
  //   7). 111 --> AND
  //   0). 000 --> ADD/SUB
  //   4). 100 --> XOR
  //   5). 101 --> SRL/SRA
  //   1). 001 --> SLL
  //   2). 010 --> SLT
  //   3). 011 --> SLTU, unsigned ADD/SUB
endmodule

module control_unit (
  input  C,
  input  R,
  input  [2:0] funct3,
  input  [8:0] inst_type_decode,
  input  b_c,
  output pc_in_en,
  output addr_inst_or_data,
  output funct3_sel,
  output rs1_sel,
  output rs2_sel,
  output funct7_sel,
  output opcode_a_sel,
  output [1:0] opcode_b_sel,
  output mem_wr_en_cntrl,
  output rf_rd_in_en,
  output data_wb_or_load,
  output [2:0] mem_strobe,
  output decode_in,
  output fetch,
  output decode_exe,
  output mem,
  output write_back,
  output J_4,
  output [1:0] inc_pc,
  output jalr,
  output j_sel
);

  wire and_2_out, b_branch, or_1_out, or_2_out, or_3_out, or_4_out, or_5_out, or_6_out, or_7_out, or_8_out,
       or_9_out, or_11_out, or_12_out, or_13_out;
  wire [1:0] adder_1_out, priority_encoder_2_out_addr, register_1_q;
  wire [2:0] and_14_out, and_16_out;
  wire [2:2] or_14_out, or_15_out;
  wire [8:0] and_1_out;
  wire [8:8] not_1_out;

  not not_1 (not_1_out[8], or_13_out);
  assign {and_1_out[8:5], jalr, inc_pc[1], b_branch, and_1_out[1:0]} = {9{not_1_out[8]}} & inst_type_decode;  // AND_Gate and_1, 9 bits wide
  or or_1 (or_1_out, and_1_out[0], and_1_out[1], b_branch, inc_pc[1], jalr, and_1_out[5], and_1_out[6], and_1_out[7], and_1_out[8]);
  or or_2 (or_2_out, and_1_out[6], and_1_out[5]);
  or or_3 (or_3_out, jalr, inc_pc[1], and_1_out[1]);
  or or_4 (or_4_out, and_1_out[0], and_1_out[1]);
  or or_5 (or_5_out, and_1_out[5], and_1_out[7]);
  priority_encoder priority_encoder_2 (
    .input0(and_1_out[8]), .input1(or_4_out), .input2(and_1_out[6]), .input3(or_5_out),
    .out_addr(priority_encoder_2_out_addr));  // open: valid
  or or_6 (or_6_out, jalr, and_1_out[0], and_1_out[1], and_1_out[5], and_1_out[7], and_1_out[8], inc_pc[1]);
  or or_7 (or_7_out, and_1_out[0], and_1_out[1]);
  or or_8 (or_8_out, and_1_out[6], b_branch, and_1_out[8]);
  and and_2 (and_2_out, ~funct3[1], funct3[0]);  // AND_Gate
  or or_9 (or_9_out, and_1_out[8], and_2_out);
  or or_10 (J_4, inc_pc[1], jalr);
  or or_11 (or_11_out, or_2_out, or_7_out);
  Adder #(.width(2)) adder_1 (.a(register_1_q), .b(2'b01), .out(adder_1_out), .cin(1'b0));  // open: cout
  or or_12 (or_12_out, or_13_out, write_back, mem);
  or or_13 (or_13_out, fetch, decode_exe);
  Register #(.width(2)) register_1 (.D(adder_1_out), .en(or_12_out), .clk(C), .Q(register_1_q), .clr(R));
  Decoder #(.enable("false"), .select(2)) decoder_1 (
    .out0(fetch), .out1(decode_exe), .out2(mem), .out3(write_back), .sel(register_1_q));
  or or_14 (or_14_out[2], write_back, mem);
  or or_15 (or_15_out[2], decode_exe, fetch);
  and and_3 (pc_in_en, write_back, or_1_out);
  and and_4 (addr_inst_or_data, or_14_out[2], or_2_out);
  and and_5 (funct3_sel, or_11_out, or_14_out[2]);
  and and_6 (rs1_sel, or_14_out[2], or_7_out);
  and and_7 (rs2_sel, or_14_out[2], or_8_out);
  and and_8 (funct7_sel, or_14_out[2], or_9_out);
  and and_9 (opcode_a_sel, or_14_out[2], or_3_out);
  assign opcode_b_sel = {2{or_14_out[2]}} & priority_encoder_2_out_addr;  // AND_Gate and_10, 2 bits wide
  and and_11 (mem_wr_en_cntrl, write_back, and_1_out[6]);
  and and_12 (rf_rd_in_en, write_back, or_6_out);
  and and_13 (data_wb_or_load, write_back, and_1_out[5]);
  assign and_14_out = {3{or_14_out[2]}} & funct3;  // AND_Gate and_14, 3 bits wide
  and and_15 (inc_pc[0], b_c, b_branch);
  or or_16 (j_sel, inc_pc[1], jalr);
  assign and_16_out = {3{or_15_out[2]}} & 3'b010;  // AND_Gate and_16, 3 bits wide
  assign mem_strobe = and_14_out | and_16_out;  // OR_Gate or_17, 3 bits wide

  assign decode_in = decode_exe;

  // Other names for the same wires on the sheet: i_jalr = jalr; j_jal = inc_pc[1]

  // Notes on the sheet:
  //   u_type_lui
  //   u_type_auipc
  //   i_type
  //   r_type
  //   i_type_load
  //   s_type_store
  //   control_micro_ops_state
  //   fetch
  //   decode/exe
  //   mem
  //   writeback
endmodule

module priority_encoder (
  input  input0,
  input  input1,
  input  input2,
  input  input3,
  output [1:0] out_addr,
  output valid
);

  wire and_1_out, not_1_out;

  not not_1 (not_1_out, input2);
  or or_1 (out_addr[1], input3, input2);
  and and_1 (and_1_out, not_1_out, input1);
  or or_2 (valid, out_addr[1], input2, input0);
  or or_3 (out_addr[0], input3, and_1_out);
endmodule

module uart_v2 (
  input  clk,
  input  rst,
  input  slave_en,
  input  [1:0] addr,
  input  [15:0] write_data,
  input  write_en,
  output [15:0] rd_data,
  output tx
);

  wire and_1_out, and_2_out, and_3_out, and_4_out, and_5_out, and_6_out, and_7_out, and_8_out, and_9_out,
       and_10_out, comparator_1_eq, decoder_1_out0, decoder_1_out2, multiplexer_3_out, multiplexer_5_out,
       nor_1_out, not_1_out, or_1_out, or_2_out, or_3_out, or_4_out, register_1_q, register_2_q, xor_1_out;
  wire [0:0] write_busy_q;
  wire [3:0] adder_2_out, multiplexer_4_out, tx_state_reg_q;
  wire [7:0] multiplexer_2_out, tx_data_reg_q;
  wire [15:0] baud_reg_q;
  wire [19:0] adder_1_out, baud_counter_q, multiplexer_1_out;

  and and_1 (and_1_out, slave_en, write_en);
  Decoder #(.enable("false"), .select(2)) decoder_1 (
    .out0(decoder_1_out0), .out2(decoder_1_out2), .sel(addr));  // open: out1, out3
  and and_2 (and_2_out, decoder_1_out2, and_1_out);
  Register #(.width(1)) write_busy (.D(and_3_out), .en(or_1_out), .clk(clk), .Q(write_busy_q[0]), .clr(rst));
  and and_3 (and_3_out, and_2_out, ~and_10_out);  // AND_Gate
  or or_1 (or_1_out, and_2_out, and_10_out);
  Adder #(.width(20)) adder_1 (.a(baud_counter_q), .b(20'h1), .out(adder_1_out), .cin(1'b0));  // open: cout
  and and_4 (and_4_out, decoder_1_out0, and_1_out);
  Multiplexer #(.width(20)) multiplexer_1 (
    .in0(adder_1_out), .in1({20{1'b0}}), .out(multiplexer_1_out), .sel(or_2_out));
  or or_2 (or_2_out, and_10_out, comparator_1_eq);
  Multiplexer #(.width(8)) multiplexer_2 (
    .in0({1'b0, tx_data_reg_q[7:1]}), .in1(write_data[7:0]), .out(multiplexer_2_out), .sel(and_2_out));
  Register #(.width(20)) baud_counter (.D(multiplexer_1_out), .en(or_3_out), .clk(clk), .Q(baud_counter_q), .clr(rst));
  or or_3 (or_3_out, write_busy_q[0], and_10_out, comparator_1_eq);
  Register #(.width(16)) baud_reg (.D(write_data), .en(and_4_out), .clk(clk), .Q(baud_reg_q), .clr(rst));
  and and_5 (and_5_out, xor_1_out, ~and_8_out);  // AND_Gate
  and and_6 (and_6_out, xor_1_out, write_busy_q[0]);
  Multiplexer multiplexer_3 (.in0(and_5_out), .in1(and_2_out), .out(multiplexer_3_out), .sel(and_7_out));
  or or_4 (or_4_out, and_6_out, and_10_out);
  Register tx_data_reg (.D(multiplexer_2_out), .en(multiplexer_3_out), .clk(clk), .Q(tx_data_reg_q), .clr(rst));
  Adder #(.width(4)) adder_2 (.a(tx_state_reg_q), .b(4'b0001), .out(adder_2_out), .cin(1'b0));  // open: cout
  Multiplexer #(.width(4)) multiplexer_4 (.in0(adder_2_out), .in1(4'b0000), .out(multiplexer_4_out), .sel(and_10_out));
  Comparator #(.mode("unsigned"), .width(20)) comparator_1 (
    .a(baud_counter_q), .b({baud_reg_q, 4'b0000}), .eq(comparator_1_eq));  // open: gt, lt
  Register #(.width(4)) tx_state_reg (.D(multiplexer_4_out), .en(or_4_out), .clk(clk), .Q(tx_state_reg_q), .clr(rst));
  Register #(.width(1)) register_1 (.D(not_1_out), .en(comparator_1_eq), .clk(clk), .Q(register_1_q), .clr(rst));
  Multiplexer multiplexer_5 (.in0(1'b1), .in1(1'b0), .out(multiplexer_5_out), .sel(and_8_out));
  Multiplexer multiplexer_6 (.in0(multiplexer_5_out), .in1(tx_data_reg_q[0]), .out(tx), .sel(nor_1_out));
  not not_1 (not_1_out, register_1_q);
  Register #(.width(1)) register_2 (.D(not_1_out), .en(write_busy_q[0]), .clk(clk), .Q(register_2_q), .clr(rst));
  nor nor_1 (nor_1_out, and_7_out, and_8_out, and_9_out, and_10_out);
  and and_7 (and_7_out, ~tx_state_reg_q[0], ~tx_state_reg_q[1], ~tx_state_reg_q[2], ~tx_state_reg_q[3]);  // AND_Gate
  and and_8 (and_8_out, tx_state_reg_q[0], ~tx_state_reg_q[1], ~tx_state_reg_q[2], ~tx_state_reg_q[3]);  // AND_Gate
  and and_9 (and_9_out, ~tx_state_reg_q[0], tx_state_reg_q[1], ~tx_state_reg_q[2], tx_state_reg_q[3]);  // AND_Gate
  and and_10 (and_10_out, tx_state_reg_q[0], tx_state_reg_q[1], ~tx_state_reg_q[2], tx_state_reg_q[3]);  // AND_Gate
  xor xor_1 (xor_1_out, not_1_out, register_2_q);
  Multiplexer #(.select(2), .width(16)) multiplexer_7 (
    .in0(baud_reg_q), .in1({16{1'b0}}), .in2({16{1'b0}}), .in3({{15{1'b0}}, write_busy_q[0]}), .out(rd_data),
    .sel(addr));

  // Other names for the same wires on the sheet: c = clk; r = rst
endmodule

module uart_v1 (
  input  clk,
  input  rst,
  input  [1:0] addr,
  input  [15:0] data_in,
  input  write_en,
  output tx
);

  wire and_1_out, and_2_out, and_3_out, and_4_out, and_5_out, and_6_out, and_7_out, comparator_1_eq,
       decoder_1_out0, decoder_1_out2, multiplexer_1_out, multiplexer_4_out, multiplexer_6_out, nor_1_out,
       not_1_out, or_1_out, or_2_out, or_3_out, or_4_out, register_1_q, register_3_q, register_4_q, xor_1_out;
  wire [3:0] adder_2_out, multiplexer_5_out, tx_state_reg_q;
  wire [7:0] multiplexer_3_out, register_2_q;
  wire [15:0] baud_reg_q;
  wire [19:0] adder_1_out, baud_counter_q, multiplexer_2_out;

  Decoder #(.enable("false"), .select(2)) decoder_1 (
    .out0(decoder_1_out0), .out2(decoder_1_out2), .sel(addr));  // open: out1, out3
  and and_1 (and_1_out, decoder_1_out2, write_en);
  Register #(.width(1)) register_1 (.D(multiplexer_1_out), .en(or_1_out), .clk(clk), .Q(register_1_q), .clr(rst));
  Multiplexer multiplexer_1 (.in0(and_1_out), .in1(1'b0), .out(multiplexer_1_out), .sel(and_7_out));
  or or_1 (or_1_out, and_1_out, and_7_out);
  Adder #(.width(20)) adder_1 (.a(baud_counter_q), .b(20'h1), .out(adder_1_out), .cin(1'b0));  // open: cout
  and and_2 (and_2_out, decoder_1_out0, write_en);
  Multiplexer #(.width(20)) multiplexer_2 (
    .in0(adder_1_out), .in1({20{1'b0}}), .out(multiplexer_2_out), .sel(or_2_out));
  or or_2 (or_2_out, and_7_out, comparator_1_eq);
  Multiplexer #(.width(8)) multiplexer_3 (
    .in0({1'b0, register_2_q[7:1]}), .in1(data_in[7:0]), .out(multiplexer_3_out), .sel(and_1_out));
  Register #(.width(20)) baud_counter (.D(multiplexer_2_out), .en(or_3_out), .clk(clk), .Q(baud_counter_q), .clr(rst));
  or or_3 (or_3_out, register_1_q, and_7_out, comparator_1_eq);
  Register #(.width(16)) baud_reg (.D(data_in), .en(and_2_out), .clk(clk), .Q(baud_reg_q), .clr(rst));
  and and_3 (and_3_out, xor_1_out, register_1_q);
  Multiplexer multiplexer_4 (.in0(xor_1_out), .in1(and_1_out), .out(multiplexer_4_out), .sel(and_4_out));
  or or_4 (or_4_out, and_3_out, and_7_out);
  Register register_2 (.D(multiplexer_3_out), .en(multiplexer_4_out), .clk(clk), .Q(register_2_q), .clr(rst));
  Adder #(.width(4)) adder_2 (.a(tx_state_reg_q), .b(4'b0001), .out(adder_2_out), .cin(1'b0));  // open: cout
  Multiplexer #(.width(4)) multiplexer_5 (.in0(adder_2_out), .in1(4'b0000), .out(multiplexer_5_out), .sel(and_7_out));
  Comparator #(.mode("unsigned"), .width(20)) comparator_1 (
    .a(baud_counter_q), .b({baud_reg_q, 4'b0000}), .eq(comparator_1_eq));  // open: gt, lt
  Register #(.width(4)) tx_state_reg (.D(multiplexer_5_out), .en(or_4_out), .clk(clk), .Q(tx_state_reg_q), .clr(rst));
  Register #(.width(1)) register_3 (.D(not_1_out), .en(comparator_1_eq), .clk(clk), .Q(register_3_q), .clr(rst));
  Multiplexer multiplexer_6 (.in0(1'b1), .in1(1'b0), .out(multiplexer_6_out), .sel(and_5_out));
  Multiplexer multiplexer_7 (.in0(multiplexer_6_out), .in1(register_2_q[0]), .out(tx), .sel(nor_1_out));
  not not_1 (not_1_out, register_3_q);
  Register #(.width(1)) register_4 (.D(not_1_out), .en(register_1_q), .clk(clk), .Q(register_4_q), .clr(rst));
  nor nor_1 (nor_1_out, and_4_out, and_5_out, and_6_out, and_7_out);
  and and_4 (and_4_out, ~tx_state_reg_q[0], ~tx_state_reg_q[1], ~tx_state_reg_q[2], ~tx_state_reg_q[3]);  // AND_Gate
  and and_5 (and_5_out, tx_state_reg_q[0], ~tx_state_reg_q[1], ~tx_state_reg_q[2], ~tx_state_reg_q[3]);  // AND_Gate
  and and_6 (and_6_out, ~tx_state_reg_q[0], tx_state_reg_q[1], ~tx_state_reg_q[2], tx_state_reg_q[3]);  // AND_Gate
  and and_7 (and_7_out, tx_state_reg_q[0], tx_state_reg_q[1], ~tx_state_reg_q[2], tx_state_reg_q[3]);  // AND_Gate
  xor xor_1 (xor_1_out, not_1_out, register_4_q);
endmodule

module gpio (
  input  clk,
  input  rst,
  input  [31:0] gpio_in,
  input  slave_en,
  input  [3:0] addr,
  input  [31:0] write_data,
  input  write_en,
  output [31:0] rd_data,
  output [31:0] gpio_out,
  output [31:0] gpio_out_en
);

  wire and_1_out, and_2_out, and_3_out, and_4_out, and_5_out, and_6_out, comparator_1_eq, register_1_q;
  wire [0:0] not_1_out;
  wire [31:0] adder_1_out, counter_q, multiplexer_1_out, reg_data_in_q;

  and and_1 (and_1_out, ~addr[0], ~addr[1], ~addr[2], ~addr[3]);  // AND_Gate
  and and_2 (and_2_out, ~addr[0], ~addr[1], addr[2], ~addr[3]);  // AND_Gate
  and and_3 (and_3_out, slave_en, write_en);
  and and_4 (and_4_out, slave_en, write_en);
  Adder #(.width(32)) adder_1 (.a(counter_q), .b(32'h1), .out(adder_1_out), .cin(1'b0));  // open: cout
  and and_5 (and_5_out, and_4_out, and_1_out);
  and and_6 (and_6_out, and_3_out, and_2_out);
  Multiplexer #(.width(32)) multiplexer_1 (
    .in0(adder_1_out), .in1({32{1'b0}}), .out(multiplexer_1_out), .sel(comparator_1_eq));
  Register #(.width(32)) counter (.D(multiplexer_1_out), .en(1'b1), .clk(clk), .Q(counter_q), .clr(rst));
  Register #(.width(32)) reg_direction (.D(write_data), .en(and_5_out), .clk(clk), .Q(gpio_out_en), .clr(rst));
  Register #(.width(32)) reg_data_out (.D(write_data), .en(and_6_out), .clk(clk), .Q(gpio_out), .clr(rst));
  Register #(.width(32)) reg_data_in (.D(gpio_in), .en(1'b1), .clk(clk), .Q(reg_data_in_q), .clr(rst));
  Comparator #(.mode("unsigned"), .width(32)) comparator_1 (
    .a(counter_q), .b(32'h17d7840), .eq(comparator_1_eq));  // open: gt, lt
  Register #(.width(1)) register_1 (.D(not_1_out[0]), .en(comparator_1_eq), .clk(clk), .Q(register_1_q), .clr(rst));
  not not_1 (not_1_out[0], register_1_q);
  Multiplexer #(.select(2), .width(32)) multiplexer_2 (
    .in0({32{1'b0}}), .in1({32{1'b0}}), .in2(reg_data_in_q), .in3({32{1'b0}}), .out(rd_data), .sel(addr[3:2]));

  // Other names for the same wires on the sheet: c = clk; r = rst
endmodule

module fast_led (
  input  clk,
  input  rst,
  input  slave_en,
  input  [2:0] addr,
  input  [23:0] write_data,
  input  write_en,
  output [7:0] rd_data,
  output fast_led_out
);

  wire and_1_out, and_2_out, and_3_out, and_4_out, and_5_out, and_6_out, and_7_out, and_8_out, and_9_out,
       and_10_out, comparator_1_eq, multiplexer_2_out, not_1_out, not_2_out, not_3_out, or_1_out, or_2_out,
       or_3_out, or_4_out, or_5_out, or_6_out, or_7_out;
  wire [1:0] write_busy_q;
  wire [4:0] adder_1_out, adder_2_out, multiplexer_3_out, multiplexer_4_out, multiplexer_5_out,
       multiplexer_6_out, seq_count_q, state_reg_q;
  wire [23:0] multiplexer_1_out, outstanding_req_data_q;
  wire [23:1] tx_data_reg_q;
  wire [23:23] tx_data_reg_q_2;

  not not_1 (not_1_out, addr[2]);
  and and_1 (and_1_out, slave_en, write_en);
  and and_2 (and_2_out, not_1_out, and_1_out);
  or or_1 (or_1_out, and_2_out, not_2_out);
  not not_2 (not_2_out, write_busy_q[0]);
  Register #(.width(24)) outstanding_req_data (
    .D(write_data), .en(and_2_out), .clk(clk), .Q(outstanding_req_data_q), .clr(rst));
  Register #(.width(1)) outstanding_en_status (.D(or_2_out), .en(or_1_out), .clk(clk), .Q(write_busy_q[1]), .clr(rst));
  or or_2 (or_2_out, and_2_out, write_busy_q[0]);
  and and_3 (and_3_out, write_busy_q[1], ~write_busy_q[0]);  // AND_Gate
  or or_3 (or_3_out, and_3_out, and_7_out);
  Register #(.width(1)) write_busy (.D(and_4_out), .en(or_3_out), .clk(clk), .Q(write_busy_q[0]), .clr(rst));
  and and_4 (and_4_out, and_3_out, ~and_7_out);  // AND_Gate
  Multiplexer #(.width(24)) multiplexer_1 (
    .in0({tx_data_reg_q, 1'b0}), .in1(outstanding_req_data_q), .out(multiplexer_1_out), .sel(and_3_out));
  Multiplexer multiplexer_2 (.in0(and_8_out), .in1(and_3_out), .out(multiplexer_2_out), .sel(and_6_out));
  Adder #(.width(5)) adder_1 (.a(state_reg_q), .b(5'b00001), .out(adder_1_out), .cin(1'b0));  // open: cout
  Register #(.width(24)) tx_data_reg (
    .D(multiplexer_1_out), .en(multiplexer_2_out), .clk(clk), .Q({tx_data_reg_q_2[23], tx_data_reg_q}),
    .clr(rst));
  Multiplexer #(.width(5)) multiplexer_3 (.in0(adder_1_out), .in1({5{1'b0}}), .out(multiplexer_3_out), .sel(and_7_out));
  and and_5 (and_5_out, write_busy_q[0], and_8_out);
  or or_4 (or_4_out, and_5_out, and_7_out);
  Register #(.width(5)) state_reg (.D(multiplexer_3_out), .en(or_4_out), .clk(clk), .Q(state_reg_q), .clr(rst));
  Adder #(.width(5)) adder_2 (.a(seq_count_q), .b(5'b00001), .out(adder_2_out), .cin(1'b0));  // open: cout
  Multiplexer #(.width(5)) multiplexer_4 (.in0(adder_2_out), .in1({5{1'b0}}), .out(multiplexer_4_out), .sel(or_5_out));
  or or_5 (or_5_out, and_8_out, and_7_out);
  and and_6 (and_6_out, ~state_reg_q[0], ~state_reg_q[1], ~state_reg_q[2], ~state_reg_q[3], ~state_reg_q[4]);  // AND_Gate
  and and_7 (and_7_out, ~state_reg_q[0], ~state_reg_q[1], ~state_reg_q[2], state_reg_q[3], state_reg_q[4]);  // AND_Gate
  Register #(.width(5)) seq_count (.D(multiplexer_4_out), .en(or_6_out), .clk(clk), .Q(seq_count_q), .clr(rst));
  or or_6 (or_6_out, and_7_out, write_busy_q[0]);
  Multiplexer #(.width(5)) multiplexer_5 (
    .in0({5{1'b0}}), .in1(multiplexer_6_out), .out(multiplexer_5_out), .sel(fast_led_out));
  Multiplexer #(.width(5)) multiplexer_6 (
    .in0(5'b01010), .in1(5'b10100), .out(multiplexer_6_out), .sel(tx_data_reg_q_2[23]));
  and and_8 (and_8_out, ~seq_count_q[0], seq_count_q[1], seq_count_q[2], seq_count_q[3], seq_count_q[4]);  // AND_Gate
  Multiplexer #(.width(8)) multiplexer_7 (
    .in0({8{1'b0}}), .in1({{6{1'b0}}, write_busy_q}), .out(rd_data), .sel(addr[2]));
  Comparator #(.mode("unsigned"), .width(5)) comparator_1 (
    .a(seq_count_q), .b(multiplexer_5_out), .eq(comparator_1_eq));  // open: gt, lt
  and and_9 (and_9_out, write_busy_q[0], comparator_1_eq);
  and and_10 (and_10_out, ~and_7_out, not_3_out);  // AND_Gate
  not not_3 (not_3_out, fast_led_out);
  or or_7 (or_7_out, and_9_out, and_7_out);
  Register #(.width(1)) register_1 (.D(and_10_out), .en(or_7_out), .clk(clk), .Q(fast_led_out), .clr(rst));

  // Other names for the same wires on the sheet: c = clk; r = rst
endmodule

module i2c (
  input  clk,
  input  rst,
  input  slave_en,
  input  read_en,
  input  [1:0] addr,
  input  [15:0] write_data,
  input  write_en,
  output [15:0] rd_data,
  output read_resp,
  output tx
);

  wire and_1_out, and_2_out, and_3_out, and_4_out, and_5_out, and_6_out, and_7_out, and_8_out, and_9_out,
       comparator_1_eq, decoder_1_out0, decoder_1_out2, multiplexer_3_out, multiplexer_5_out, nor_1_out,
       not_1_out, or_1_out, or_2_out, or_3_out, register_1_q, register_2_q, xor_1_out;
  wire [0:0] undriven;
  wire [3:0] adder_2_out, multiplexer_4_out, tx_state_reg_q;
  wire [7:0] multiplexer_2_out, tx_data_reg_q;
  wire [15:0] multiplexer_7_out, prescaler_reg_q;
  wire [19:0] adder_1_out, multiplexer_1_out, prescaler_counter_q;

  and and_1 (and_1_out, slave_en, read_en);
  and and_2 (and_2_out, slave_en, write_en);
  Decoder #(.enable("false"), .select(2)) decoder_1 (
    .out0(decoder_1_out0), .out2(decoder_1_out2), .sel(addr));  // open: out1, out3
  and and_3 (and_3_out, decoder_1_out2, and_2_out);
  Adder #(.width(20)) adder_1 (.a(prescaler_counter_q), .b(20'h1), .out(adder_1_out), .cin(1'b0));  // open: cout
  and and_4 (and_4_out, decoder_1_out0, and_2_out);
  Multiplexer #(.width(20)) multiplexer_1 (
    .in0(adder_1_out), .in1({20{1'b0}}), .out(multiplexer_1_out), .sel(or_1_out));
  or or_1 (or_1_out, and_9_out, comparator_1_eq);
  Multiplexer #(.width(8)) multiplexer_2 (
    .in0({1'b0, tx_data_reg_q[7:1]}), .in1(write_data[7:0]), .out(multiplexer_2_out), .sel(and_3_out));
  Register #(.width(20)) prescaler_counter (
    .D(multiplexer_1_out), .en(or_2_out), .clk(clk), .Q(prescaler_counter_q), .clr(rst));
  or or_2 (or_2_out, undriven[0], and_9_out, comparator_1_eq);
  Register #(.width(16)) prescaler_reg (.D(write_data), .en(and_4_out), .clk(clk), .Q(prescaler_reg_q), .clr(rst));
  and and_5 (and_5_out, xor_1_out, undriven[0]);
  Multiplexer multiplexer_3 (.in0(xor_1_out), .in1(and_3_out), .out(multiplexer_3_out), .sel(and_6_out));
  or or_3 (or_3_out, and_5_out, and_9_out);
  Register tx_data_reg (.D(multiplexer_2_out), .en(multiplexer_3_out), .clk(clk), .Q(tx_data_reg_q), .clr(rst));
  Adder #(.width(4)) adder_2 (.a(tx_state_reg_q), .b(4'b0001), .out(adder_2_out), .cin(1'b0));  // open: cout
  Multiplexer #(.width(4)) multiplexer_4 (.in0(adder_2_out), .in1(4'b0000), .out(multiplexer_4_out), .sel(and_9_out));
  Comparator #(.mode("unsigned"), .width(20)) comparator_1 (
    .a(prescaler_counter_q), .b({prescaler_reg_q, 4'b0000}), .eq(comparator_1_eq));  // open: gt, lt
  Register #(.width(4)) tx_state_reg (.D(multiplexer_4_out), .en(or_3_out), .clk(clk), .Q(tx_state_reg_q), .clr(rst));
  Register #(.width(1)) register_1 (.D(not_1_out), .en(comparator_1_eq), .clk(clk), .Q(register_1_q), .clr(rst));
  Multiplexer multiplexer_5 (.in0(1'b1), .in1(1'b0), .out(multiplexer_5_out), .sel(and_7_out));
  Multiplexer multiplexer_6 (.in0(multiplexer_5_out), .in1(tx_data_reg_q[0]), .out(tx), .sel(nor_1_out));
  not not_1 (not_1_out, register_1_q);
  Register #(.width(1)) register_2 (.D(not_1_out), .en(undriven[0]), .clk(clk), .Q(register_2_q), .clr(rst));
  nor nor_1 (nor_1_out, and_6_out, and_7_out, and_8_out, and_9_out);
  and and_6 (and_6_out, ~tx_state_reg_q[0], ~tx_state_reg_q[1], ~tx_state_reg_q[2], ~tx_state_reg_q[3]);  // AND_Gate
  and and_7 (and_7_out, tx_state_reg_q[0], ~tx_state_reg_q[1], ~tx_state_reg_q[2], ~tx_state_reg_q[3]);  // AND_Gate
  and and_8 (and_8_out, ~tx_state_reg_q[0], tx_state_reg_q[1], ~tx_state_reg_q[2], tx_state_reg_q[3]);  // AND_Gate
  and and_9 (and_9_out, tx_state_reg_q[0], tx_state_reg_q[1], ~tx_state_reg_q[2], tx_state_reg_q[3]);  // AND_Gate
  xor xor_1 (xor_1_out, not_1_out, register_2_q);
  Multiplexer #(.select(2), .width(16)) multiplexer_7 (
    .in0(prescaler_reg_q), .in1({16{1'b0}}), .in2({16{1'b0}}), .in3({{15{1'b0}}, undriven[0]}),
    .out(multiplexer_7_out), .sel(addr));
  Register #(.width(16)) register_3 (.D(multiplexer_7_out), .en(and_1_out), .clk(clk), .Q(rd_data), .clr(rst));
  Register #(.width(1)) register_4 (.D(and_1_out), .en(1'b1), .clk(clk), .Q(read_resp), .clr(rst));

  // Other names for the same wires on the sheet: c = clk; r = rst
endmodule

module memory (
  input  [31:0] data_in,
  input  [13:0] addr,
  input  slave_en,
  input  wr_en,
  input  [2:0] strobe,
  input  clk,
  output [31:0] data_out
);

  wire and_1_out, and_2_out, and_3_out, and_4_out, and_5_out;
  wire [1:1] decoder_2_out0, decoder_2_out1;
  wire [3:0] decoder_1_out0, multiplexer_1_out;
  wire [7:0] multiplexer_3_out;
  wire [15:0] bank0_dout, bank2_dout, multiplexer_2_out;
  wire [31:0] shifter_1_out, zero_sign_extend_8_1_outp, zero_sign_extend_16_1_outp;

  Shifter #(.width(32)) shifter_1 (.in(data_in), .\dist ({addr[1:0], 3'b000}), .out(shifter_1_out));
  and and_1 (and_1_out, slave_en, wr_en);
  RAM #(.addrWidth(12), .asyncread("true")) bank3 (
    .addr(addr[13:2]), .we(and_2_out), .oe(1'b1), .clk(clk), .din(shifter_1_out[31:24]),
    .dout(bank2_dout[15:8]));
  Decoder #(.enable("false"), .select(2)) decoder_1 (
    .out0(decoder_1_out0[0]), .out1(decoder_1_out0[1]), .out2(decoder_1_out0[2]), .out3(decoder_1_out0[3]),
    .sel(addr[1:0]));
  Decoder #(.enable("false")) decoder_2 (.out0(decoder_2_out0[1]), .out1(decoder_2_out1[1]), .sel(addr[1]));
  and and_2 (and_2_out, and_1_out, multiplexer_1_out[3]);
  Multiplexer #(.select(2), .width(4)) multiplexer_1 (
    .in0(decoder_1_out0), .in1({{2{decoder_2_out1[1]}}, {2{decoder_2_out0[1]}}}), .in2(4'b1111),
    .in3(4'b0000), .out(multiplexer_1_out), .sel(strobe[1:0]));
  RAM #(.addrWidth(12), .asyncread("true")) bank2 (
    .addr(addr[13:2]), .we(and_3_out), .oe(1'b1), .clk(clk), .din(shifter_1_out[23:16]),
    .dout(bank2_dout[7:0]));
  and and_3 (and_3_out, and_1_out, multiplexer_1_out[2]);
  Multiplexer #(.width(16)) multiplexer_2 (.in0(bank0_dout), .in1(bank2_dout), .out(multiplexer_2_out), .sel(addr[1]));
  Multiplexer #(.select(2), .width(8)) multiplexer_3 (
    .in0(bank0_dout[7:0]), .in1(bank0_dout[15:8]), .in2(bank2_dout[7:0]), .in3(bank2_dout[15:8]),
    .out(multiplexer_3_out), .sel(addr[1:0]));
  RAM #(.addrWidth(12), .asyncread("true")) bank1 (
    .addr(addr[13:2]), .we(and_4_out), .oe(1'b1), .clk(clk), .din(shifter_1_out[15:8]),
    .dout(bank0_dout[15:8]));
  and and_4 (and_4_out, and_1_out, multiplexer_1_out[1]);
  zero_sign_extend_16 zero_sign_extend_16_1 (
    .inpt(multiplexer_2_out), .sign_ext_en(strobe[2]), .outp(zero_sign_extend_16_1_outp));
  zero_sign_extend_8 zero_sign_extend_8_1 (
    .inpt(multiplexer_3_out), .sign_ext_en(strobe[2]), .outp(zero_sign_extend_8_1_outp));
  Multiplexer #(.select(2), .width(32)) multiplexer_4 (
    .in0(zero_sign_extend_8_1_outp), .in1(zero_sign_extend_16_1_outp), .in2({bank2_dout, bank0_dout}),
    .in3({32{1'b0}}), .out(data_out), .sel(strobe[1:0]));
  // Probe on data_out
  RAM #(.addrWidth(12), .asyncread("true")) bank0 (
    .addr(addr[13:2]), .we(and_5_out), .oe(1'b1), .clk(clk), .din(shifter_1_out[7:0]), .dout(bank0_dout[7:0]));
  and and_5 (and_5_out, and_1_out, multiplexer_1_out[0]);
endmodule

module memory_rtl_synth (
  input  [31:0] data_in,
  input  [13:0] addr,
  input  slave_en,
  input  wr_en,
  input  [2:0] strobe,
  input  clk,
  output [31:0] data_out
);

  wire and_1_out, and_2_out, and_3_out, and_4_out, and_5_out;
  wire [1:1] decoder_2_out0, decoder_2_out1;
  wire [3:0] decoder_1_out0, multiplexer_1_out;
  wire [7:0] multiplexer_3_out;
  wire [15:0] bram_bank_0_do, bram_bank_2_do, multiplexer_2_out;
  wire [31:0] shifter_1_out, zero_sign_extend_8_1_outp, zero_sign_extend_16_1_outp;

  Shifter #(.width(32)) shifter_1 (.in(data_in), .\dist ({addr[1:0], 3'b000}), .out(shifter_1_out));
  and and_1 (and_1_out, slave_en, wr_en);
  Decoder #(.enable("false"), .select(2)) decoder_1 (
    .out0(decoder_1_out0[0]), .out1(decoder_1_out0[1]), .out2(decoder_1_out0[2]), .out3(decoder_1_out0[3]),
    .sel(addr[1:0]));
  Decoder #(.enable("false")) decoder_2 (.out0(decoder_2_out0[1]), .out1(decoder_2_out1[1]), .sel(addr[1]));
  and and_2 (and_2_out, and_1_out, multiplexer_1_out[3]);
  bram_place_holder bram_bank_3 (
    .A(addr[13:2]), .WE(and_2_out), .clk(clk), .DI(shifter_1_out[31:24]), .DO(bram_bank_2_do[15:8]));
  Multiplexer #(.select(2), .width(4)) multiplexer_1 (
    .in0(decoder_1_out0), .in1({{2{decoder_2_out1[1]}}, {2{decoder_2_out0[1]}}}), .in2(4'b1111),
    .in3(4'b0000), .out(multiplexer_1_out), .sel(strobe[1:0]));
  and and_3 (and_3_out, and_1_out, multiplexer_1_out[2]);
  bram_place_holder bram_bank_2 (
    .A(addr[13:2]), .WE(and_3_out), .clk(clk), .DI(shifter_1_out[23:16]), .DO(bram_bank_2_do[7:0]));
  Multiplexer #(.width(16)) multiplexer_2 (
    .in0(bram_bank_0_do), .in1(bram_bank_2_do), .out(multiplexer_2_out), .sel(addr[1]));
  Multiplexer #(.select(2), .width(8)) multiplexer_3 (
    .in0(bram_bank_0_do[7:0]), .in1(bram_bank_0_do[15:8]), .in2(bram_bank_2_do[7:0]),
    .in3(bram_bank_2_do[15:8]), .out(multiplexer_3_out), .sel(addr[1:0]));
  and and_4 (and_4_out, and_1_out, multiplexer_1_out[1]);
  zero_sign_extend_16 zero_sign_extend_16_1 (
    .inpt(multiplexer_2_out), .sign_ext_en(strobe[2]), .outp(zero_sign_extend_16_1_outp));
  bram_place_holder bram_bank_1 (
    .A(addr[13:2]), .WE(and_4_out), .clk(clk), .DI(shifter_1_out[15:8]), .DO(bram_bank_0_do[15:8]));
  zero_sign_extend_8 zero_sign_extend_8_1 (
    .inpt(multiplexer_3_out), .sign_ext_en(strobe[2]), .outp(zero_sign_extend_8_1_outp));
  Multiplexer #(.select(2), .width(32)) multiplexer_4 (
    .in0(zero_sign_extend_8_1_outp), .in1(zero_sign_extend_16_1_outp),
    .in2({bram_bank_2_do, bram_bank_0_do}), .in3({32{1'b0}}), .out(data_out), .sel(strobe[1:0]));
  // Probe on data_out
  and and_5 (and_5_out, and_1_out, multiplexer_1_out[0]);
  bram_place_holder bram_bank_0 (
    .A(addr[13:2]), .WE(and_5_out), .clk(clk), .DI(shifter_1_out[7:0]), .DO(bram_bank_0_do[7:0]));
endmodule

module bram_place_holder (
  input  [11:0] A,
  input  WE,
  input  clk,
  input  [7:0] DI,
  output [7:0] DO
);


  assign DO = {8{1'b0}};
endmodule

module zero_sign_extend_8 (
  input  [7:0] inpt,
  input  sign_ext_en,
  output [31:0] outp
);

  and and_1 (outp[31], inpt[7], sign_ext_en);

  assign outp[30:0] = {{24{outp[31]}}, inpt[6:0]};
endmodule

module zero_sign_extend_16 (
  input  [15:0] inpt,
  input  sign_ext_en,
  output [31:0] outp
);

  and and_1 (outp[31], inpt[15], sign_ext_en);

  assign outp[30:0] = {{16{outp[31]}}, inpt[14:0]};
endmodule

module zero_detection (
  input  [31:0] data,
  output ZERO
);

  nor nor_1 (ZERO, data[0], data[1], data[2], data[3], data[4], data[5], data[6], data[7], data[8], data[9], data[10], data[11], data[12], data[13], data[14], data[15], data[16], data[17], data[18], data[19], data[20], data[21], data[22], data[23], data[24], data[25], data[26], data[27], data[28], data[29], data[30], data[31]);
endmodule

module alu_v2 (
  input  [31:0] a_input,
  input  [31:0] b_input,
  input  func_7,
  input  [2:0] func_3,
  output ZERO,
  output [31:0] ALU_OUT
);

  wire adder_v1_1_sof, adder_v1_1_sum_32, adder_v1_1_uof, not_1_out, not_2_out, or_2_out;
  wire [0:0] and_2_out, and_3_out;
  wire [31:0] adder_v1_1_sum, and_1_out, multiplexer_1_out, or_1_out, shifter_1_out, shifter_2_out,
       shifter_3_out, xor_1_out;

  // Probe on a_input
  // Probe on a_input
  // Probe on a_input
  Shifter #(.shift("lr"), .width(32)) shifter_1 (.in(a_input), .\dist (b_input[4:0]), .out(shifter_1_out));
  Shifter #(.shift("ar"), .width(32)) shifter_2 (.in(a_input), .\dist (b_input[4:0]), .out(shifter_2_out));
  // Probe on b_input
  Shifter #(.width(32)) shifter_3 (.in(a_input), .\dist (b_input[4:0]), .out(shifter_3_out));
  assign xor_1_out = b_input ^ a_input;  // XOR_Gate xor_1, 32 bits wide
  assign or_1_out = a_input | b_input;  // OR_Gate or_1, 32 bits wide
  assign and_1_out = a_input & b_input;  // AND_Gate and_1, 32 bits wide
  // Probe on b_input
  // Probe on b_input
  adder_v1 adder_v1_1 (
    .func7(func_7), .a(a_input), .b(b_input), .sum(adder_v1_1_sum), .sum_32(adder_v1_1_sum_32),
    .sof(adder_v1_1_sof), .uof(adder_v1_1_uof));
  not not_1 (not_1_out, adder_v1_1_sof);
  not not_2 (not_2_out, adder_v1_1_uof);
  Multiplexer #(.width(32)) multiplexer_1 (
    .in0(shifter_1_out), .in1(shifter_2_out), .out(multiplexer_1_out), .sel(func_7));
  and and_2 (and_2_out[0], adder_v1_1_sum[31], not_1_out);
  or or_2 (or_2_out, adder_v1_1_sum[31], adder_v1_1_sum_32);
  and and_3 (and_3_out[0], or_2_out, not_2_out);
  // Probe on adder_v1_1_sum
  // Probe on adder_v1_1_sum
  Multiplexer #(.select(3), .width(32)) multiplexer_2 (
    .in0(adder_v1_1_sum), .in1(shifter_3_out), .in2({{31{1'b0}}, and_2_out[0]}),
    .in3({{31{1'b0}}, and_3_out[0]}), .in4(xor_1_out), .in5(multiplexer_1_out), .in6(or_1_out),
    .in7(and_1_out), .out(ALU_OUT), .sel(func_3));
  nor nor_1 (ZERO, ALU_OUT[0], ALU_OUT[1], ALU_OUT[2], ALU_OUT[3], ALU_OUT[4], ALU_OUT[5], ALU_OUT[6], ALU_OUT[7], ALU_OUT[8], ALU_OUT[9], ALU_OUT[10], ALU_OUT[11], ALU_OUT[12], ALU_OUT[13], ALU_OUT[14], ALU_OUT[15], ALU_OUT[16], ALU_OUT[17], ALU_OUT[18], ALU_OUT[19], ALU_OUT[20], ALU_OUT[21], ALU_OUT[22], ALU_OUT[23], ALU_OUT[24], ALU_OUT[25], ALU_OUT[26], ALU_OUT[27], ALU_OUT[28], ALU_OUT[29], ALU_OUT[30], ALU_OUT[31]);

  // Notes on the sheet:
  //   1). 001 --> SLL
  //   4). 100 --> XOR
  //   6). 110 --> OR
  //   7). 111 --> AND
  //   0). 000 --> ADD/SUB, 2). 010 --> SLT
  //   3). 011 --> SLTU, unsigned ADD/SUB
  //   5). 101 --> SRL/SRA
endmodule

module adder_v1 (
  input  func7,
  input  [31:0] a,
  input  [31:0] b,
  output [31:0] sum,
  output sum_32,
  output sof,
  output uof
);

  wire adder_1_cout, adder_2_cout;
  wire [32:0] multiplexer_1_out, not_1_out;

  assign not_1_out = ~{1'b0, b};  // NOT_Gate not_1, 33 bits wide
  Multiplexer #(.width(33)) multiplexer_1 (.in0({1'b0, b}), .in1(not_1_out), .out(multiplexer_1_out), .sel(func7));
  Adder #(.width(31)) adder_1 (
    .a(a[30:0]), .b(multiplexer_1_out[30:0]), .out(sum[30:0]), .cin(func7), .cout(adder_1_cout));
  Adder #(.width(1)) adder_2 (
    .a(a[31]), .b(multiplexer_1_out[31]), .out(sum[31]), .cin(adder_1_cout), .cout(adder_2_cout));
  Adder #(.width(1)) adder_3 (.a(1'b0), .b(multiplexer_1_out[32]), .out(sum_32), .cin(adder_2_cout), .cout(uof));
  xor xor_1 (sof, adder_1_cout, adder_2_cout);
endmodule

module adder_v1_test (
  input  [31:0] a,
  input  [31:0] b,
  input  func7,
  input  in_4,
  input  in_5,
  input  in_6,
  output [31:0] sum,
  output signed_overflow,
  output sltu
);

  wire adder_1_cout, adder_2_cout, clock_1_out, comparator_1_lt, controlled_buffer_1_out, xnor_1_out;
  wire [31:0] random_1_out, random_2_out, register_1_q, register_2_q;
  wire [32:0] multiplexer_1_out, not_1_out;

  Random #(.width(32)) random_1 (.clr(in_4), .next(xnor_1_out), .clk(controlled_buffer_1_out), .out(random_1_out));
  Random #(.width(32)) random_2 (.clr(in_6), .next(xnor_1_out), .clk(controlled_buffer_1_out), .out(random_2_out));
  Register #(.width(32)) register_1 (
    .D(random_1_out), .en(xnor_1_out), .clk(controlled_buffer_1_out), .Q(register_1_q), .clr(in_5));
  Register #(.width(32)) register_2 (
    .D(random_2_out), .en(xnor_1_out), .clk(controlled_buffer_1_out), .Q(register_2_q), .clr(in_5));
  assign controlled_buffer_1_out = xnor_1_out ? clock_1_out : 1'bz;  // Controlled_Buffer controlled_buffer_1
  Clock clock_1 (.out(clock_1_out));
  assign not_1_out = ~{1'b0, register_2_q};  // NOT_Gate not_1, 33 bits wide
  Multiplexer #(.width(33)) multiplexer_1 (
    .in0({1'b0, register_2_q}), .in1(not_1_out), .out(multiplexer_1_out), .sel(func7));
  Adder #(.width(31)) adder_1 (
    .a(register_1_q[30:0]), .b(multiplexer_1_out[30:0]), .out(sum[30:0]), .cin(func7), .cout(adder_1_cout));
  Adder #(.width(1)) adder_2 (
    .a(register_1_q[31]), .b(multiplexer_1_out[31]), .out(sum[31]), .cin(adder_1_cout), .cout(adder_2_cout));
  Adder #(.width(1)) adder_3 (.a(1'b0), .b(multiplexer_1_out[32]), .out(sltu), .cin(adder_2_cout));  // open: cout
  xor xor_1 (signed_overflow, adder_1_cout, adder_2_cout);
  Comparator #(.mode("unsigned"), .width(32)) comparator_1 (
    .a(register_1_q), .b(register_2_q), .lt(comparator_1_lt));  // open: gt, eq
  Register #(.width(1)) register_3 (.D(xnor_1_out), .en(1'b1), .clk(clock_1_out));  // open: Q, clr
  xnor xnor_1 (xnor_1_out, sltu, comparator_1_lt);
endmodule

module clock_divider_by2 (
  input  clk_in,
  input  rst,
  output clk_out
);

  wire not_1_out;

  Register #(.width(1)) register_1 (.D(not_1_out), .en(1'b1), .clk(clk_in), .Q(clk_out), .clr(rst));
  not not_1 (not_1_out, clk_out);
endmodule

module reset_synchronizer (
  input  clk,
  input  rst_in,
  output rst_out
);

  wire register_1_q;

  Register #(.width(1)) register_1 (.D(1'b1), .en(1'b1), .clk(clk), .Q(register_1_q), .clr(rst_in));
  Register #(.width(1)) register_2 (.D(register_1_q), .en(1'b1), .clk(clk), .Q(rst_out), .clr(rst_in));
endmodule

module gpio_buffer (
  input  [19:0] data_in,
  input  [19:0] data_en,
  output [19:0] data_out
);

  assign data_out[0] = data_en[0] ? data_in[0] : 1'bz;  // Controlled_Buffer controlled_buffer_1
  assign data_out[1] = data_en[1] ? data_in[1] : 1'bz;  // Controlled_Buffer controlled_buffer_2
  assign data_out[2] = data_en[2] ? data_in[2] : 1'bz;  // Controlled_Buffer controlled_buffer_3
  assign data_out[3] = data_en[3] ? data_in[3] : 1'bz;  // Controlled_Buffer controlled_buffer_4
  assign data_out[4] = data_en[4] ? data_in[4] : 1'bz;  // Controlled_Buffer controlled_buffer_5
  assign data_out[5] = data_en[5] ? data_in[5] : 1'bz;  // Controlled_Buffer controlled_buffer_6
  assign data_out[6] = data_en[6] ? data_in[6] : 1'bz;  // Controlled_Buffer controlled_buffer_7
  assign data_out[7] = data_en[7] ? data_in[7] : 1'bz;  // Controlled_Buffer controlled_buffer_8
  assign data_out[8] = data_en[8] ? data_in[8] : 1'bz;  // Controlled_Buffer controlled_buffer_9
  assign data_out[9] = data_en[9] ? data_in[9] : 1'bz;  // Controlled_Buffer controlled_buffer_10
  assign data_out[10] = data_en[10] ? data_in[10] : 1'bz;  // Controlled_Buffer controlled_buffer_11
  assign data_out[11] = data_en[11] ? data_in[11] : 1'bz;  // Controlled_Buffer controlled_buffer_12
  assign data_out[12] = data_en[12] ? data_in[12] : 1'bz;  // Controlled_Buffer controlled_buffer_13
  assign data_out[13] = data_en[13] ? data_in[13] : 1'bz;  // Controlled_Buffer controlled_buffer_14
  assign data_out[14] = data_en[14] ? data_in[14] : 1'bz;  // Controlled_Buffer controlled_buffer_15
  assign data_out[15] = data_en[15] ? data_in[15] : 1'bz;  // Controlled_Buffer controlled_buffer_16
  assign data_out[16] = data_en[16] ? data_in[16] : 1'bz;  // Controlled_Buffer controlled_buffer_17
  assign data_out[17] = data_en[17] ? data_in[17] : 1'bz;  // Controlled_Buffer controlled_buffer_18
  assign data_out[18] = data_en[18] ? data_in[18] : 1'bz;  // Controlled_Buffer controlled_buffer_19
  assign data_out[19] = data_en[19] ? data_in[19] : 1'bz;  // Controlled_Buffer controlled_buffer_20
endmodule
